# Fritzing sketch Esquematico (saved by Fritzing 0.9.4)
breadboards: 1

parts:
  4_Channel_Relay1 = 4 Channel Power Relay
  Componente1 = Bluetooth HC-05 Macho
  Componente2 = Arduino Uno (Rev3) - ICSP
  BULB1 = Incandescent light bulb small [package="bulb sm"]
  BULB2 = Incandescent light bulb small [package="bulb sm"]
  BULB3 = Incandescent light bulb small [package="bulb sm"]
  BULB4 = Incandescent light bulb small [package="bulb sm"]
  Sensor2 = TTP223B Capacitive Touch Sensor Module
  Part3 = Lilypad Battery Connect
  Part4 = Lilypad Battery Connect
  Part5 = Lilypad Battery Connect
  Part6 = Lilypad Battery Connect
  HC-SR04_Sensor_1 = HC-SR04 Ultrasonic Distance Sensor
  J2 = DHT11 basic temperature-humidity sensor [form="♂ (male)" package=THT]

nets:
  GND: 4_Channel_Relay1.GND, Componente1.GND, Componente2.GND, Sensor2.GND, HC-SR04_Sensor_1.GND, J2.GND
  N1: 4_Channel_Relay1.IN1, Componente2.D6_PWM
  N2: 4_Channel_Relay1.IN2, Componente2.D7
  N3: 4_Channel_Relay1.IN3, Componente2.D8
  N4: 4_Channel_Relay1.IN4, Componente2.D9_PWM
  VCC: 4_Channel_Relay1.VCC, Componente1.VCC, Componente2.5V, Sensor2.VCC, HC-SR04_Sensor_1.VCC, J2.VCC
  N5: 4_Channel_Relay1.COM#17, Part3.+
  N6: 4_Channel_Relay1.NO#18, BULB1.2
  N7: 4_Channel_Relay1.COM#20, Part4.+
  N8: 4_Channel_Relay1.NO#21, BULB2.2
  N9: 4_Channel_Relay1.COM#23, Part5.+
  N10: 4_Channel_Relay1.NO#24, BULB3.2
  N11: 4_Channel_Relay1.COM#26, Part6.+
  N12: 4_Channel_Relay1.NO#27, BULB4.2
  N13: Componente1.TXD, Componente2.D0/RX
  N14: Componente1.RXD, Componente2.D1/TX
  N15: Componente2.A0, J2.OUT
  N16: Componente2.D12/MISO, HC-SR04_Sensor_1.TRIG
  N17: Componente2.D13/SCK, HC-SR04_Sensor_1.ECHO
  N18: Componente2.D2, Sensor2.SIG
  N19: BULB1.1, Part3.-
  N20: BULB2.1, Part4.-
  N21: BULB3.1, Part5.-
  N22: BULB4.1, Part6.-

notes:
  Sensor Touch Capacitivo TTP223b en la alcoba.
  Toma de 120V AC
  Sensor Ultrasónico (proximidad) en el comedor.
  Sensor de temperatura y humedad DHT11.

custom parts:
  4 Channel Power Relay: A 4 channel power relay. The module operates at 5V.
  TTP223B Capacitive Touch Sensor Module: The TTP223B capacitive touch sensor module uses the TTP223B IC. The appropriate voltage is approximately 2 to 5.5 volts.
  DHT11 basic temperature-humidity sensor: The DHT11 is a basic, ultra low-cost digital temperature and humidity sensor. It uses a capacitive humidity sensor and a thermistor to measure the surrounding air, and spits out a digital signal on the data pin (no analog input pins needed). Its fairly simple to use, but requires careful timing to grab data. The only real downside of this sensor is you can only get new data from it once every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
